# Fritzing sketch smart_stairs (saved by Fritzing 0.9.3b)

parts:
  Part1 = Arduino Uno (Rev3)
  Part2 = SRF05 Ultrasonic Rangefinder
  Part3 = SRF05 Ultrasonic Rangefinder
  PS1 = prefix0000 [part_number="12v Power Supply"]
  U3 = SK6812 RGBW LED Strip
  U4 = SK6812 RGBW LED Strip
  U5 = SK6812 RGBW LED Strip
  U6 = SK6812 RGBW LED Strip
  U7 = SK6812 RGBW LED Strip
  U8 = SK6812 RGBW LED Strip
  U9 = SK6812 RGBW LED Strip
  U10 = SK6812 RGBW LED Strip
  U11 = SK6812 RGBW LED Strip
  U12 = SK6812 RGBW LED Strip
  U13 = SK6812 RGBW LED Strip
  U14 = SK6812 RGBW LED Strip
  U15 = SK6812 RGBW LED Strip
  U18 = SK6812 RGBW LED Strip
  U20 = SK6812 RGBW LED Strip
  U22 = SK6812 RGBW LED Strip
  U23 = SK6812 RGBW LED Strip
  Q4 = MOSFET-NCHANNEL [package=to220v]

nets:
  N1: Part1.D9_PWM, Q4.G
  N2: Part1.D10_PWM/SS, Part3.Trig
  N3: Part1.D11_PWM/MOSI, Part3.Echo
  N4: Part1.D12/MISO, Part2.Trig
  N5: Part1.D13/SCK, Part2.Echo
  GND: Part1.GND, Part2.GND, Part3.GND, PS1.connector4, Q4.S
  VCC: Part1.5V, Part2.VCC, Part3.VCC
  +5V: PS1.connector1, U3.+5V, U4.+5V, U5.+5V, U6.+5V, U7.+5V, U8.+5V, U9.+5V, U10.+5V, U11.+5V, U12.+5V, U13.+5V, U14.+5V, U15.+5V, U18.+5V, U20.+5V, U22.+5V, U23.+5V
  GND_2: U3.GND, U5.GND, U6.GND, U7.GND, U8.GND, U9.GND, U10.GND, U11.GND, U13.GND, U14.GND, U15.GND, U18.GND, U20.GND, U22.GND, Q4.D

custom parts:
  SK6812 RGBW LED Strip: SK6812 RGBW Strip
